# Fritzing sketch ArdBot01 (saved by Fritzing 0.9.2b)
breadboards: 1

parts:
  Part1 = Arduino Nano (Rev3.0)
  U1 = SWITCH_SPDT [package=kps-1290]
  PIEZO_SPEAKER = Piezo Speaker
  VCC1 = Battery
  VCC2 = Battery
  LEFT = Basic Servo
  BAT1 = BC9VPC [package=bc9vpc]
  RIGHT = Basic Servo
  IR_RECV = TSOP312.., 314.. [package=THT]
  MICRO_LEAF_SWITCH_R = Momentary Switch [package=ksa_sealed_tac_switch]
  MICRO_LEAF_SWITCH_L = Momentary Switch [package=ksa_sealed_tac_switch]

nets:
  GND: Part1.GND, U1.O, VCC2.-, LEFT.gnd
  N1: Part1.D2, MICRO_LEAF_SWITCH_L.4
  N2: Part1.D3, MICRO_LEAF_SWITCH_R.2
  N3: Part1.D4, MICRO_LEAF_SWITCH_R.4, MICRO_LEAF_SWITCH_L.2
  N4: Part1.D5, IR_RECV.Data
  N5: Part1.D6, IR_RECV.Vs
  N6: Part1.D7, IR_RECV.GND
  N7: Part1.D8, RIGHT.pulse
  N8: Part1.D9, LEFT.pulse
  N9: Part1.D11/MOSI, PIEZO_SPEAKER.pin1
  N10: Part1.D12/MISO, PIEZO_SPEAKER.pin2
  N11: Part1.VIN, BAT1.V-
  N12: Part1.5V, U1.P, BAT1.V+
  N13: VCC1.+, LEFT.vcc

notes:
  6V (~4.8V)
